// Logisim project 8bit_processor_1.circ as structural Verilog: 2 circuits, main circuit main
module main (
);

  wire alu_1_s8, alu_1_s9, alu_1_s10, alu_1_s11, alu_1_s12, alu_1_s13, alu_1_s14, alu_1_s15, and_1_out,
       and_2_out, and_3_out, and_4_out, and_5_out, and_7_out, and_9_out, and_10_out, and_14_out, and_16_out,
       and_17_out, and_23_out, and_24_out, and_26_out, and_27_out, and_28_out, and_29_out, and_30_out,
       and_31_out, and_32_out, button_1_out, button_2_out, button_3_out, clock_1_out,
       controlled_buffer_2_out, controlled_buffer_3_out, controlled_buffer_4_out, controlled_buffer_5_out,
       controlled_buffer_6_out, controlled_buffer_7_out, controlled_buffer_8_out, controlled_buffer_9_out,
       j_k_ff_1_q, keyboard_1_avail, n7414_1_pin2, n7414_1_pin8, n74161_1_pin2, n74161_1_pin7,
       n74161_1_pin10, n74161_2_pin2, n74161_2_pin10, n74161_2_pin11, n74161_2_pin12, n74161_2_pin13,
       n74161_2_pin14, n74161_2_pin15, n74161_3_pin11, n74161_3_pin12, n74161_3_pin13, n74161_3_pin14,
       n74161_4_pin10, n74161_4_pin11, n74161_4_pin12, n74161_4_pin13, n74161_4_pin14, n74161_5_pin11,
       n74161_5_pin12, n74161_5_pin13, n74161_5_pin14, n74161_7_pin1, n74161_7_pin10, n74161_7_pin15,
       n74161_8_pin13, n74161_9_pin1, n74161_9_pin15, n74161_10_pin12, n74161_11_pin9, n74161_11_pin10,
       n74161_11_pin15, n74161_12_pin9, n74161_12_pin15, n74161_13_pin9, n74161_13_pin10, n74161_13_pin15,
       n74161_14_pin9, n74161_14_pin15, n74165_1_pin1, n74165_1_pin15, n74175_1_pin2, n74175_1_pin7,
       n74175_1_pin9, n74175_1_pin10, n74175_1_pin15, n74193_1_pin4, n74193_1_pin5, n74193_1_pin11,
       n74193_1_pin14, n74193_2_pin4, n74193_2_pin5, n74245_10_pin11, n74245_10_pin12, n74245_10_pin13,
       n74245_10_pin14, n74245_10_pin15, n74245_10_pin16, n74245_10_pin17, n74245_10_pin18, n74245_11_pin11,
       n74245_11_pin12, n74245_11_pin13, n74245_11_pin14, n74245_11_pin15, n74245_11_pin16, n74245_11_pin17,
       n74245_11_pin18, n74245_12_pin11, n74245_12_pin12, n74245_12_pin13, n74245_12_pin14, n74245_12_pin15,
       n74245_12_pin16, n74245_12_pin17, n74245_12_pin18, n74245_13_pin11, n74245_13_pin12, n74245_13_pin13,
       n74245_13_pin14, n74245_13_pin15, n74245_13_pin16, n74245_13_pin17, n74245_13_pin18, n74245_14_pin2,
       n74245_14_pin3, n74245_14_pin4, n74245_14_pin5, n74245_14_pin6, n74245_14_pin7, n74245_14_pin8,
       n74245_14_pin9, n74245_16_pin11, n74245_16_pin12, n74245_16_pin13, n74245_16_pin14, n74245_16_pin15,
       n74245_16_pin16, n74245_16_pin17, n74245_16_pin18, n74245_17_pin11, n74245_17_pin12, n74245_17_pin13,
       n74245_17_pin14, n74245_17_pin15, n74245_17_pin16, n74245_17_pin17, n74245_17_pin18, n74245_18_pin11,
       n74245_18_pin12, n74245_18_pin13, n74245_18_pin14, n74245_18_pin15, n74245_18_pin16, n74245_18_pin17,
       n74245_18_pin18, n74245_20_pin11, n74245_20_pin12, n74245_20_pin13, n74245_20_pin14, n74245_20_pin15,
       n74245_20_pin16, n74245_20_pin17, n74245_20_pin18, n74245_21_pin11, n74245_21_pin12, n74245_21_pin13,
       n74245_21_pin14, n74245_21_pin15, n74245_21_pin16, n74245_21_pin17, n74245_21_pin18, n74273_1_pin3,
       n74273_1_pin4, n74273_1_pin7, n74273_1_pin8, n74273_1_pin13, n74273_1_pin14, n74273_1_pin17,
       n74273_1_pin18, n74273_2_pin2, n74273_2_pin3, n74273_2_pin4, n74273_2_pin5, n74273_2_pin6,
       n74273_2_pin7, n74273_2_pin8, n74273_2_pin9, n74273_2_pin12, n74273_2_pin13, n74273_2_pin14,
       n74273_2_pin15, n74273_2_pin16, n74273_2_pin17, n74273_2_pin18, n74273_2_pin19, n74273_3_pin3,
       n74273_3_pin4, n74273_3_pin7, n74273_3_pin8, n74273_3_pin13, n74273_3_pin14, n74273_3_pin17,
       n74273_3_pin18, n74273_4_pin2, n74273_4_pin3, n74273_4_pin4, n74273_4_pin5, n74273_4_pin6,
       n74273_4_pin7, n74273_4_pin8, n74273_4_pin9, n74273_4_pin12, n74273_4_pin13, n74273_4_pin14,
       n74273_4_pin15, n74273_4_pin16, n74273_4_pin17, n74273_4_pin18, n74273_4_pin19, n74273_5_pin3,
       n74273_5_pin4, n74273_5_pin7, n74273_5_pin8, n74273_5_pin13, n74273_5_pin14, n74273_5_pin17,
       n74273_5_pin18, n74273_6_pin11, n74273_7_pin11, n74273_8_pin11, n74273_9_pin2, n74273_9_pin5,
       n74273_9_pin6, n74273_9_pin9, n74273_9_pin12, n74273_9_pin15, n74273_9_pin16, n74273_9_pin19,
       n74273_10_pin2, n74273_10_pin5, n74273_10_pin6, n74273_10_pin9, n74273_10_pin11, n74273_10_pin12,
       n74273_10_pin15, n74273_10_pin16, n74273_10_pin19, n74273_11_pin11, n74273_13_pin2, n74273_13_pin5,
       n74273_13_pin6, n74273_13_pin9, n74273_13_pin11, n74273_13_pin12, n74273_13_pin15, n74273_13_pin16,
       n74273_13_pin19, n74273_14_pin2, n74273_14_pin5, n74273_14_pin6, n74273_14_pin9, n74273_14_pin11,
       n74273_14_pin12, n74273_14_pin15, n74273_14_pin16, n74273_14_pin19, n74273_15_pin2, n74273_15_pin3,
       n74273_15_pin4, n74273_15_pin5, nor_2_out, nor_3_out, not_1_out, not_2_out, not_3_out, not_4_out,
       not_5_out, not_7_out, not_8_out, not_9_out, not_10_out, not_11_out, not_12_out, not_13_out,
       not_14_out, not_15_out, not_16_out, not_17_out, not_18_out, not_19_out, not_20_out, not_21_out,
       not_22_out, or_1_out, or_2_out, or_3_out, or_4_out, or_5_out, or_6_out, or_7_out, or_8_out, or_12_out,
       or_13_out, rgb_video_1_p2, rgb_video_1_p3, rgb_video_2_p3, s_r_ff_1_q, s_r_ff_2_q, s_r_ff_3_q,
       s_r_ff_5_q, undriven;
  wire [1:0] alu_1_cf, alu_1_zf;
  wire [3:0] n74273_7_pin9, n74273_7_pin19, n74273_11_pin9, n74273_11_pin19;
  wire [3:3] rgb_video_1_p6;
  wire [4:0] n74161_6_pin14, rgb_video_1_p5, rgb_video_2_p7;
  wire [5:0] rgb_video_1_p4, rgb_video_2_p6;
  wire [6:0] keyboard_1_data;
  wire [7:0] controlled_buffer_1_out, n74165_1_pin11, n74245_4_pin9, n74273_5_pin2, n74273_6_pin19,
       ram_2_dout;
  wire [8:0] rom_2_data;
  wire [13:13] and_6_out;
  wire [15:0] n74273_3_pin2;
  wire [63:0] rom_1_data;

  Button button_1 (.out(button_1_out));
  Button button_2 (.out(button_2_out));
  or or_1 (or_1_out, button_1_out, button_2_out);
  Button button_3 (.out(button_3_out));
  // RGB_Video #(.cursor("No Cursor"), .height(32), .scale(8), .width(64)) rgb_video_1: pin names not known; wires that end beside it: or_1_out, rgb_video_1_p2, rgb_video_1_p3, rgb_video_1_p4, rgb_video_1_p5, {4{rgb_video_1_p6[3]}}
  _74165 #(.ShowInternalStructure("true")) u_74165_1 (
    .pin1(n74165_1_pin1), .pin2(rgb_video_1_p2), .pin3(n74165_1_pin11[4]), .pin4(n74165_1_pin11[5]),
    .pin5(n74165_1_pin11[6]), .pin6(n74165_1_pin11[7]), .pin15(n74165_1_pin15), .pin14(n74165_1_pin11[3]),
    .pin13(n74165_1_pin11[2]), .pin12(n74165_1_pin11[1]), .pin11(n74165_1_pin11[0]), .pin9(rgb_video_1_p6[3]));  // open: pin7, pin10
  nor nor_1 (n74165_1_pin1, ~rgb_video_1_p3, n74165_1_pin15, and_9_out);  // NOR_Gate
  or or_2 (or_2_out, button_3_out, rom_1_data[54]);
  Clock clock_1 (.out(clock_1_out));
  RAM #(.asyncread("true"), .\type ("nonvolatile")) ram_1 (
    .addr(n74273_6_pin19), .we(rom_1_data[55]), .oe(n74161_1_pin7), .clk(rgb_video_1_p2),
    .din(controlled_buffer_1_out), .dout(n74165_1_pin11));
  not not_1 (not_1_out, s_r_ff_1_q);
  S_R_Flip_Flop s_r_ff_1 (
    .S(rom_1_data[60]), .clk(rgb_video_1_p2), .R(rom_1_data[53]), .Q(s_r_ff_1_q), .reset(or_1_out));  // open: Qn, preset
  and and_1 (and_1_out, rom_1_data[51], rgb_video_1_p2);
  not not_2 (not_2_out, rgb_video_1_p3);
  Keyboard keyboard_1 (
    .clk(rgb_video_1_p2), .re(rom_1_data[60]), .clr(or_1_out), .avail(keyboard_1_avail),
    .data(keyboard_1_data));
  not not_3 (not_3_out, keyboard_1_avail);
  and and_2 (and_2_out, clock_1_out, ~rom_1_data[1]);  // AND_Gate
  and and_3 (and_3_out, rom_1_data[47], rgb_video_1_p2);
  RAM #(.addrWidth(16), .asyncread("true"), .\type ("nonvolatile")) ram_2 (
    .addr(n74273_3_pin2), .we(rom_1_data[48]), .oe(rom_1_data[49]), .clk(rgb_video_1_p2),
    .din(n74245_4_pin9), .dout(ram_2_dout));
  and and_4 (and_4_out, rgb_video_1_p2, rom_1_data[50]);
  S_R_Flip_Flop s_r_ff_2 (.Q(s_r_ff_2_q), .reset(or_3_out), .preset(or_2_out));  // open: S, R, clk, Qn
  J_K_Flip_Flop j_k_ff_1 (
    .J(keyboard_1_avail), .K(not_3_out), .clk(rgb_video_1_p2), .Q(j_k_ff_1_q));  // open: Qn, preset, reset
  not not_4 (not_4_out, n7414_1_pin8);
  nor nor_2 (nor_2_out, not_4_out, rom_1_data[62]);
  not not_5 (not_5_out, rom_1_data[63]);
  _7414 u_7414_1 (
    .pin1(and_2_out), .pin2(n7414_1_pin2), .pin3(n7414_1_pin2), .pin4(rgb_video_1_p2), .pin5(n74165_1_pin15),
    .pin13(n74165_1_pin15), .pin11(n74165_1_pin15), .pin9(or_1_out), .pin8(n7414_1_pin8));  // open: pin6, pin12, pin10
  _74273 u_74273_1 (
    .pin1(n7414_1_pin8), .pin2(n74273_3_pin2[8]), .pin3(n74273_1_pin3), .pin4(n74273_1_pin4),
    .pin5(n74273_3_pin2[9]), .pin6(n74273_3_pin2[10]), .pin7(n74273_1_pin7), .pin8(n74273_1_pin8),
    .pin9(n74273_3_pin2[11]), .pin19(n74273_3_pin2[15]), .pin18(n74273_1_pin18), .pin17(n74273_1_pin17),
    .pin16(n74273_3_pin2[14]), .pin15(n74273_3_pin2[13]), .pin14(n74273_1_pin14), .pin13(n74273_1_pin13),
    .pin12(n74273_3_pin2[12]), .pin11(and_3_out));
  _74273 u_74273_2 (
    .pin1(n7414_1_pin8), .pin2(n74273_2_pin2), .pin3(n74273_2_pin3), .pin4(n74273_2_pin4),
    .pin5(n74273_2_pin5), .pin6(n74273_2_pin6), .pin7(n74273_2_pin7), .pin8(n74273_2_pin8),
    .pin9(n74273_2_pin9), .pin19(n74273_2_pin19), .pin18(n74273_2_pin18), .pin17(n74273_2_pin17),
    .pin16(n74273_2_pin16), .pin15(n74273_2_pin15), .pin14(n74273_2_pin14), .pin13(n74273_2_pin13),
    .pin12(n74273_2_pin12), .pin11(and_1_out));
  S_R_Flip_Flop s_r_ff_3 (
    .S(s_r_ff_2_q), .R(n74165_1_pin15), .clk(rgb_video_1_p2), .Q(s_r_ff_3_q), .reset(or_4_out));  // open: Qn, preset
  or or_3 (or_3_out, s_r_ff_3_q, or_1_out);
  or or_4 (or_4_out, or_1_out, and_10_out);
  _74161 u_74161_1 (
    .pin1(nor_2_out), .pin2(n74161_1_pin2), .pin7(n74161_1_pin7), .pin14(n74161_6_pin14[4]),
    .pin10(n74161_1_pin10));  // open: pin3, pin4, pin5, pin6, pin15, pin13, pin12, pin11, pin9
  not not_6 (n74161_1_pin2, rgb_video_1_p2);
  or or_5 (or_5_out, rgb_video_1_p3, s_r_ff_2_q);
  or or_6 (or_6_out, s_r_ff_3_q, and_10_out);
  nor nor_3 (nor_3_out, or_1_out, rom_1_data[57]);
  assign controlled_buffer_1_out[6:0] = rom_1_data[61] ? keyboard_1_data : 7'bz;  // Controlled_Buffer controlled_buffer_1
  not not_7 (not_7_out, rom_1_data[45]);
  not not_8 (not_8_out, rom_1_data[44]);
  and and_5 (and_5_out, rgb_video_1_p2, rom_1_data[46]);
  _74245 u_74245_1 (
    .pin1(n74161_1_pin7), .pin2(controlled_buffer_1_out[0]), .pin3(controlled_buffer_1_out[1]),
    .pin4(controlled_buffer_1_out[2]), .pin5(controlled_buffer_1_out[3]), .pin6(controlled_buffer_1_out[4]),
    .pin7(controlled_buffer_1_out[5]), .pin8(controlled_buffer_1_out[6]), .pin9(controlled_buffer_1_out[7]),
    .pin19(n74165_1_pin15), .pin18(n74273_1_pin3), .pin17(n74273_1_pin4), .pin16(n74273_1_pin7),
    .pin15(n74273_1_pin8), .pin14(n74273_1_pin13), .pin13(n74273_1_pin14), .pin12(n74273_1_pin17),
    .pin11(n74273_1_pin18));
  _74245 u_74245_2 (
    .pin1(n74161_1_pin7), .pin2(controlled_buffer_1_out[0]), .pin3(controlled_buffer_1_out[1]),
    .pin4(controlled_buffer_1_out[2]), .pin5(controlled_buffer_1_out[3]), .pin6(controlled_buffer_1_out[4]),
    .pin7(controlled_buffer_1_out[5]), .pin8(controlled_buffer_1_out[6]), .pin9(controlled_buffer_1_out[7]),
    .pin19(n74165_1_pin15), .pin18(n74273_2_pin3), .pin17(n74273_2_pin4), .pin16(n74273_2_pin7),
    .pin15(n74273_2_pin8), .pin14(n74273_2_pin13), .pin13(n74273_2_pin14), .pin12(n74273_2_pin17),
    .pin11(n74273_2_pin18));
  _74161 u_74161_2 (
    .pin1(n7414_1_pin8), .pin2(n74161_2_pin2), .pin7(or_6_out), .pin15(n74161_2_pin15),
    .pin14(n74161_2_pin14), .pin13(n74161_2_pin13), .pin12(n74161_2_pin12), .pin11(n74161_2_pin11),
    .pin10(n74161_2_pin10), .pin9(n7414_1_pin8));  // open: pin3, pin4, pin5, pin6
  _74161 u_74161_3 (
    .pin1(n7414_1_pin8), .pin2(n74161_2_pin2), .pin7(or_6_out), .pin15(n74161_2_pin10),
    .pin14(n74161_3_pin14), .pin13(n74161_3_pin13), .pin12(n74161_3_pin12), .pin11(n74161_3_pin11),
    .pin10(n7414_1_pin8), .pin9(n7414_1_pin8));  // open: pin3, pin4, pin5, pin6
  _74161 u_74161_4 (
    .pin1(nor_3_out), .pin2(rgb_video_1_p2), .pin7(rom_1_data[58]), .pin14(n74161_4_pin14),
    .pin13(n74161_4_pin13), .pin12(n74161_4_pin12), .pin11(n74161_4_pin11), .pin10(n74161_4_pin10),
    .pin9(n74161_1_pin7));  // open: pin3, pin4, pin5, pin6, pin15
  _74161 u_74161_5 (
    .pin1(nor_3_out), .pin2(rgb_video_1_p2), .pin7(rom_1_data[58]), .pin15(n74161_4_pin10),
    .pin14(n74161_5_pin14), .pin13(n74161_5_pin13), .pin12(n74161_5_pin12), .pin11(n74161_5_pin11),
    .pin10(n74161_1_pin7), .pin9(n74161_1_pin7));  // open: pin3, pin4, pin5, pin6
  and and_6 (and_6_out[13], not_5_out, not_1_out, j_k_ff_1_q);
  _74161 u_74161_6 (
    .pin1(nor_2_out), .pin2(n74161_1_pin2), .pin7(n74161_1_pin7), .pin15(n74161_1_pin10),
    .pin14(n74161_6_pin14[0]), .pin13(n74161_6_pin14[1]), .pin12(n74161_6_pin14[2]),
    .pin11(n74161_6_pin14[3]), .pin10(n74161_1_pin7));  // open: pin3, pin4, pin5, pin6, pin9
  and and_7 (and_7_out, rgb_video_1_p2, rom_1_data[52]);
  _74161 u_74161_7 (
    .pin1(n74161_7_pin1), .pin2(rgb_video_1_p2), .pin7(rgb_video_1_p3), .pin15(n74161_7_pin15),
    .pin14(rgb_video_1_p5[0]), .pin13(rgb_video_1_p5[1]), .pin12(rgb_video_1_p5[2]),
    .pin11(rgb_video_1_p5[3]), .pin10(n74161_7_pin10), .pin9(n74161_1_pin7));  // open: pin3, pin4, pin5, pin6
  not not_9 (not_9_out, n74161_8_pin13);
  and and_8 (n74161_7_pin1, not_9_out, ~or_1_out);  // AND_Gate
  _74161 u_74161_8 (
    .pin1(n74161_7_pin1), .pin2(rgb_video_1_p2), .pin7(rgb_video_1_p3), .pin14(rgb_video_1_p5[4]),
    .pin13(n74161_8_pin13), .pin10(n74161_7_pin15), .pin9(n74161_1_pin7));  // open: pin3, pin4, pin5, pin6, pin15, pin12, pin11
  or or_7 (or_7_out, or_1_out, n74161_8_pin13);
  S_R_Flip_Flop s_r_ff_4 (.Q(rgb_video_1_p3), .reset(or_7_out), .preset(s_r_ff_3_q));  // open: S, R, clk, Qn
  assign controlled_buffer_2_out = or_5_out ? n74161_2_pin14 : 1'bz;  // Controlled_Buffer controlled_buffer_2
  assign controlled_buffer_3_out = or_5_out ? n74161_2_pin13 : 1'bz;  // Controlled_Buffer controlled_buffer_3
  assign controlled_buffer_4_out = or_5_out ? n74161_2_pin12 : 1'bz;  // Controlled_Buffer controlled_buffer_4
  assign controlled_buffer_5_out = or_5_out ? n74161_2_pin11 : 1'bz;  // Controlled_Buffer controlled_buffer_5
  assign controlled_buffer_6_out = or_5_out ? n74161_3_pin14 : 1'bz;  // Controlled_Buffer controlled_buffer_6
  assign controlled_buffer_7_out = or_5_out ? n74161_3_pin13 : 1'bz;  // Controlled_Buffer controlled_buffer_7
  assign controlled_buffer_8_out = or_5_out ? n74161_3_pin12 : 1'bz;  // Controlled_Buffer controlled_buffer_8
  assign controlled_buffer_9_out = or_5_out ? n74161_3_pin11 : 1'bz;  // Controlled_Buffer controlled_buffer_9
  assign controlled_buffer_9_out = rom_1_data[56] ? n74161_5_pin11 : 1'bz;  // Controlled_Buffer controlled_buffer_10
  assign controlled_buffer_8_out = rom_1_data[56] ? n74161_5_pin12 : 1'bz;  // Controlled_Buffer controlled_buffer_11
  assign controlled_buffer_7_out = rom_1_data[56] ? n74161_5_pin13 : 1'bz;  // Controlled_Buffer controlled_buffer_12
  not not_10 (not_10_out, rom_1_data[33]);
  not not_11 (not_11_out, rom_1_data[32]);
  not not_12 (not_12_out, rom_1_data[27]);
  not not_13 (not_13_out, n74161_2_pin2);
  and and_9 (and_9_out, not_13_out, s_r_ff_5_q);
  S_R_Flip_Flop s_r_ff_5 (.Q(s_r_ff_5_q), .reset(and_9_out), .preset(n74161_2_pin2));  // open: S, R, clk, Qn
  and and_10 (and_10_out, n74161_2_pin10, n74161_2_pin15);
  assign controlled_buffer_6_out = rom_1_data[56] ? n74161_5_pin14 : 1'bz;  // Controlled_Buffer controlled_buffer_13
  assign controlled_buffer_2_out = rom_1_data[56] ? n74161_4_pin14 : 1'bz;  // Controlled_Buffer controlled_buffer_14
  assign controlled_buffer_3_out = rom_1_data[56] ? n74161_4_pin13 : 1'bz;  // Controlled_Buffer controlled_buffer_15
  assign controlled_buffer_4_out = rom_1_data[56] ? n74161_4_pin12 : 1'bz;  // Controlled_Buffer controlled_buffer_16
  ROM #(.addrWidth(14), .dataWidth(64)) rom_1 (
    .addr({and_6_out[13], n74273_5_pin2, n74161_6_pin14}), .data(rom_1_data));
  not not_14 (not_14_out, rom_1_data[26]);
  not not_15 (not_15_out, rom_1_data[23]);
  not not_16 (not_16_out, rom_1_data[19]);
  _74273 u_74273_3 (
    .pin1(n7414_1_pin8), .pin2(n74273_3_pin2[0]), .pin3(n74273_3_pin3), .pin4(n74273_3_pin4),
    .pin5(n74273_3_pin2[1]), .pin6(n74273_3_pin2[2]), .pin7(n74273_3_pin7), .pin8(n74273_3_pin8),
    .pin9(n74273_3_pin2[3]), .pin19(n74273_3_pin2[7]), .pin18(n74273_3_pin18), .pin17(n74273_3_pin17),
    .pin16(n74273_3_pin2[6]), .pin15(n74273_3_pin2[5]), .pin14(n74273_3_pin14), .pin13(n74273_3_pin13),
    .pin12(n74273_3_pin2[4]), .pin11(and_5_out));
  not not_17 (not_17_out, rom_1_data[49]);
  _74245 u_74245_3 (
    .pin1(n74161_1_pin7), .pin2(ram_2_dout[7]), .pin3(ram_2_dout[6]), .pin4(ram_2_dout[5]),
    .pin5(ram_2_dout[4]), .pin6(ram_2_dout[3]), .pin7(ram_2_dout[2]), .pin8(ram_2_dout[1]),
    .pin9(ram_2_dout[0]), .pin19(not_17_out), .pin18(controlled_buffer_1_out[7]),
    .pin17(controlled_buffer_1_out[6]), .pin16(controlled_buffer_1_out[5]),
    .pin15(controlled_buffer_1_out[4]), .pin14(controlled_buffer_1_out[3]),
    .pin13(controlled_buffer_1_out[2]), .pin12(controlled_buffer_1_out[1]), .pin11(controlled_buffer_1_out[0]));
  not not_18 (not_18_out, rom_1_data[48]);
  _74245 u_74245_4 (
    .pin1(n74165_1_pin15), .pin2(n74245_4_pin9[7]), .pin3(n74245_4_pin9[6]), .pin4(n74245_4_pin9[5]),
    .pin5(n74245_4_pin9[4]), .pin6(n74245_4_pin9[3]), .pin7(n74245_4_pin9[2]), .pin8(n74245_4_pin9[1]),
    .pin9(n74245_4_pin9[0]), .pin19(not_18_out), .pin18(controlled_buffer_1_out[7]),
    .pin17(controlled_buffer_1_out[6]), .pin16(controlled_buffer_1_out[5]),
    .pin15(controlled_buffer_1_out[4]), .pin14(controlled_buffer_1_out[3]),
    .pin13(controlled_buffer_1_out[2]), .pin12(controlled_buffer_1_out[1]), .pin11(controlled_buffer_1_out[0]));
  _74273 u_74273_4 (
    .pin1(n7414_1_pin8), .pin2(n74273_4_pin2), .pin3(n74273_4_pin3), .pin4(n74273_4_pin4),
    .pin5(n74273_4_pin5), .pin6(n74273_4_pin6), .pin7(n74273_4_pin7), .pin8(n74273_4_pin8),
    .pin9(n74273_4_pin9), .pin19(n74273_4_pin19), .pin18(n74273_4_pin18), .pin17(n74273_4_pin17),
    .pin16(n74273_4_pin16), .pin15(n74273_4_pin15), .pin14(n74273_4_pin14), .pin13(n74273_4_pin13),
    .pin12(n74273_4_pin12), .pin11(and_4_out));
  _74273 u_74273_5 (
    .pin1(n7414_1_pin8), .pin2(n74273_5_pin2[0]), .pin3(n74273_5_pin3), .pin4(n74273_5_pin4),
    .pin5(n74273_5_pin2[1]), .pin6(n74273_5_pin2[2]), .pin7(n74273_5_pin7), .pin8(n74273_5_pin8),
    .pin9(n74273_5_pin2[3]), .pin19(n74273_5_pin2[7]), .pin18(n74273_5_pin18), .pin17(n74273_5_pin17),
    .pin16(n74273_5_pin2[6]), .pin15(n74273_5_pin2[5]), .pin14(n74273_5_pin14), .pin13(n74273_5_pin13),
    .pin12(n74273_5_pin2[4]), .pin11(and_7_out));
  _74273 u_74273_6 (
    .pin1(n7414_1_pin8), .pin2(n74273_6_pin19[7]), .pin3(controlled_buffer_5_out),
    .pin4(controlled_buffer_4_out), .pin5(n74273_6_pin19[6]), .pin6(n74273_6_pin19[5]),
    .pin7(controlled_buffer_3_out), .pin8(controlled_buffer_2_out), .pin9(n74273_6_pin19[4]),
    .pin19(n74273_6_pin19[0]), .pin18(controlled_buffer_6_out), .pin17(controlled_buffer_7_out),
    .pin16(n74273_6_pin19[1]), .pin15(n74273_6_pin19[2]), .pin14(controlled_buffer_8_out),
    .pin13(controlled_buffer_9_out), .pin12(n74273_6_pin19[3]), .pin11(n74273_6_pin11));
  assign controlled_buffer_5_out = rom_1_data[56] ? n74161_4_pin11 : 1'bz;  // Controlled_Buffer controlled_buffer_17
  not not_19 (not_19_out, rom_1_data[11]);
  _74161 u_74161_9 (
    .pin1(n74161_9_pin1), .pin2(rgb_video_1_p2), .pin7(rgb_video_1_p3), .pin15(n74161_9_pin15),
    .pin14(rgb_video_1_p4[0]), .pin13(rgb_video_1_p4[1]), .pin12(rgb_video_1_p4[2]),
    .pin11(rgb_video_1_p4[3]), .pin10(n74161_1_pin7), .pin9(n74161_1_pin7));  // open: pin3, pin4, pin5, pin6
  and and_11 (n74161_9_pin1, ~n74161_10_pin12, ~or_1_out);  // AND_Gate
  _74161 u_74161_10 (
    .pin1(n74161_9_pin1), .pin2(rgb_video_1_p2), .pin7(rgb_video_1_p3), .pin14(rgb_video_1_p4[4]),
    .pin13(rgb_video_1_p4[5]), .pin12(n74161_10_pin12), .pin10(n74161_9_pin15), .pin9(n74161_1_pin7));  // open: pin3, pin4, pin5, pin6, pin15, pin11
  not not_20 (not_20_out, rom_1_data[10]);
  not not_21 (not_21_out, rom_1_data[5]);
  not not_22 (not_22_out, rom_1_data[4]);
  _74245 u_74245_5 (
    .pin1(n74161_1_pin7), .pin2(controlled_buffer_1_out[0]), .pin3(controlled_buffer_1_out[1]),
    .pin4(controlled_buffer_1_out[2]), .pin5(controlled_buffer_1_out[3]), .pin6(controlled_buffer_1_out[4]),
    .pin7(controlled_buffer_1_out[5]), .pin8(controlled_buffer_1_out[6]), .pin9(controlled_buffer_1_out[7]),
    .pin19(n74165_1_pin15), .pin18(n74273_3_pin3), .pin17(n74273_3_pin4), .pin16(n74273_3_pin7),
    .pin15(n74273_3_pin8), .pin14(n74273_3_pin13), .pin13(n74273_3_pin14), .pin12(n74273_3_pin17),
    .pin11(n74273_3_pin18));
  _74245 u_74245_6 (
    .pin1(n74161_1_pin7), .pin2(controlled_buffer_1_out[0]), .pin3(controlled_buffer_1_out[1]),
    .pin4(controlled_buffer_1_out[2]), .pin5(controlled_buffer_1_out[3]), .pin6(controlled_buffer_1_out[4]),
    .pin7(controlled_buffer_1_out[5]), .pin8(controlled_buffer_1_out[6]), .pin9(controlled_buffer_1_out[7]),
    .pin19(n74165_1_pin15), .pin18(n74273_4_pin3), .pin17(n74273_4_pin4), .pin16(n74273_4_pin7),
    .pin15(n74273_4_pin8), .pin14(n74273_4_pin13), .pin13(n74273_4_pin14), .pin12(n74273_4_pin17),
    .pin11(n74273_4_pin18));
  _74245 u_74245_7 (
    .pin1(n74165_1_pin15), .pin2(controlled_buffer_1_out[0]), .pin3(controlled_buffer_1_out[1]),
    .pin4(controlled_buffer_1_out[2]), .pin5(controlled_buffer_1_out[3]), .pin6(controlled_buffer_1_out[4]),
    .pin7(controlled_buffer_1_out[5]), .pin8(controlled_buffer_1_out[6]), .pin9(controlled_buffer_1_out[7]),
    .pin19(not_22_out), .pin18(n74273_4_pin2), .pin17(n74273_4_pin5), .pin16(n74273_4_pin6),
    .pin15(n74273_4_pin9), .pin14(n74273_4_pin12), .pin13(n74273_4_pin15), .pin12(n74273_4_pin16),
    .pin11(n74273_4_pin19));
  _74245 u_74245_8 (
    .pin1(n74165_1_pin15), .pin2(controlled_buffer_1_out[0]), .pin3(controlled_buffer_1_out[1]),
    .pin4(controlled_buffer_1_out[2]), .pin5(controlled_buffer_1_out[3]), .pin6(controlled_buffer_1_out[4]),
    .pin7(controlled_buffer_1_out[5]), .pin8(controlled_buffer_1_out[6]), .pin9(controlled_buffer_1_out[7]),
    .pin19(not_21_out), .pin18(n74273_2_pin2), .pin17(n74273_2_pin5), .pin16(n74273_2_pin6),
    .pin15(n74273_2_pin9), .pin14(n74273_2_pin12), .pin13(n74273_2_pin15), .pin12(n74273_2_pin16),
    .pin11(n74273_2_pin19));
  _74245 u_74245_9 (
    .pin1(n74161_1_pin7), .pin2(controlled_buffer_1_out[0]), .pin3(controlled_buffer_1_out[1]),
    .pin4(controlled_buffer_1_out[2]), .pin5(controlled_buffer_1_out[3]), .pin6(controlled_buffer_1_out[4]),
    .pin7(controlled_buffer_1_out[5]), .pin8(controlled_buffer_1_out[6]), .pin9(controlled_buffer_1_out[7]),
    .pin19(n74165_1_pin15), .pin18(n74273_5_pin3), .pin17(n74273_5_pin4), .pin16(n74273_5_pin7),
    .pin15(n74273_5_pin8), .pin14(n74273_5_pin13), .pin13(n74273_5_pin14), .pin12(n74273_5_pin17),
    .pin11(n74273_5_pin18));
  and and_12 (n74161_2_pin2, rgb_video_1_p4[0], rgb_video_1_p4[1], rgb_video_1_p4[2]);
  or or_8 (or_8_out, s_r_ff_2_q, rgb_video_1_p3);
  Pull_Resistor pull_resistor_1 (.node(controlled_buffer_1_out[7]));
  and and_13 (n74161_7_pin10, rgb_video_1_p4[0], rgb_video_1_p4[1], rgb_video_1_p4[2], rgb_video_1_p4[3], rgb_video_1_p4[4], rgb_video_1_p4[5]);
  and and_14 (and_14_out, or_8_out, ~rgb_video_1_p2);  // AND_Gate
  or or_9 (n74273_6_pin11, rom_1_data[59], and_14_out);
  Pull_Resistor pull_resistor_2 (.node(controlled_buffer_1_out[6]));
  Pull_Resistor pull_resistor_3 (.node(controlled_buffer_1_out[5]));
  Pull_Resistor pull_resistor_4 (.node(controlled_buffer_1_out[4]));
  Pull_Resistor pull_resistor_5 (.node(controlled_buffer_1_out[3]));
  Pull_Resistor pull_resistor_6 (.node(controlled_buffer_1_out[2]));
  Pull_Resistor pull_resistor_7 (.node(controlled_buffer_1_out[1]));
  Pull_Resistor pull_resistor_8 (.node(controlled_buffer_1_out[0]));
  _74245 u_74245_10 (
    .pin1(n74165_1_pin15), .pin2(controlled_buffer_1_out[0]), .pin3(controlled_buffer_1_out[1]),
    .pin4(controlled_buffer_1_out[2]), .pin5(controlled_buffer_1_out[3]), .pin6(controlled_buffer_1_out[4]),
    .pin7(controlled_buffer_1_out[5]), .pin8(controlled_buffer_1_out[6]), .pin9(controlled_buffer_1_out[7]),
    .pin19(not_7_out), .pin18(n74245_10_pin18), .pin17(n74245_10_pin17), .pin16(n74245_10_pin16),
    .pin15(n74245_10_pin15), .pin14(n74245_10_pin14), .pin13(n74245_10_pin13), .pin12(n74245_10_pin12),
    .pin11(n74245_10_pin11));
  _74245 u_74245_11 (
    .pin1(n74165_1_pin15), .pin2(controlled_buffer_1_out[0]), .pin3(controlled_buffer_1_out[1]),
    .pin4(controlled_buffer_1_out[2]), .pin5(controlled_buffer_1_out[3]), .pin6(controlled_buffer_1_out[4]),
    .pin7(controlled_buffer_1_out[5]), .pin8(controlled_buffer_1_out[6]), .pin9(controlled_buffer_1_out[7]),
    .pin19(not_8_out), .pin18(n74245_11_pin18), .pin17(n74245_11_pin17), .pin16(n74245_11_pin16),
    .pin15(n74245_11_pin15), .pin14(n74245_11_pin14), .pin13(n74245_11_pin13), .pin12(n74245_11_pin12),
    .pin11(n74245_11_pin11));
  _74245 u_74245_12 (
    .pin1(n74161_1_pin7), .pin2(controlled_buffer_1_out[7]), .pin3(controlled_buffer_1_out[6]),
    .pin4(controlled_buffer_1_out[5]), .pin5(controlled_buffer_1_out[4]), .pin6(controlled_buffer_1_out[3]),
    .pin7(controlled_buffer_1_out[2]), .pin8(controlled_buffer_1_out[1]), .pin9(controlled_buffer_1_out[0]),
    .pin19(n74165_1_pin15), .pin18(n74245_12_pin18), .pin17(n74245_12_pin17), .pin16(n74245_12_pin16),
    .pin15(n74245_12_pin15), .pin14(n74245_12_pin14), .pin13(n74245_12_pin13), .pin12(n74245_12_pin12),
    .pin11(n74245_12_pin11));
  _74245 u_74245_13 (
    .pin1(n74161_1_pin7), .pin2(controlled_buffer_1_out[7]), .pin3(controlled_buffer_1_out[6]),
    .pin4(controlled_buffer_1_out[5]), .pin5(controlled_buffer_1_out[4]), .pin6(controlled_buffer_1_out[3]),
    .pin7(controlled_buffer_1_out[2]), .pin8(controlled_buffer_1_out[1]), .pin9(controlled_buffer_1_out[0]),
    .pin19(n74165_1_pin15), .pin18(n74245_13_pin18), .pin17(n74245_13_pin17), .pin16(n74245_13_pin16),
    .pin15(n74245_13_pin15), .pin14(n74245_13_pin14), .pin13(n74245_13_pin13), .pin12(n74245_13_pin12),
    .pin11(n74245_13_pin11));
  _74245 u_74245_14 (
    .pin1(n74161_1_pin7), .pin2(n74245_14_pin2), .pin3(n74245_14_pin3), .pin4(n74245_14_pin4),
    .pin5(n74245_14_pin5), .pin6(n74245_14_pin6), .pin7(n74245_14_pin7), .pin8(n74245_14_pin8),
    .pin9(n74245_14_pin9), .pin19(not_15_out), .pin18(controlled_buffer_1_out[7]),
    .pin17(controlled_buffer_1_out[6]), .pin16(controlled_buffer_1_out[5]),
    .pin15(controlled_buffer_1_out[4]), .pin14(controlled_buffer_1_out[3]),
    .pin13(controlled_buffer_1_out[2]), .pin12(controlled_buffer_1_out[1]), .pin11(controlled_buffer_1_out[0]));
  _74245 u_74245_15 (
    .pin1(n74165_1_pin15), .pin2(controlled_buffer_1_out[7]), .pin3(controlled_buffer_1_out[6]),
    .pin4(controlled_buffer_1_out[5]), .pin5(controlled_buffer_1_out[4]), .pin6(controlled_buffer_1_out[3]),
    .pin7(controlled_buffer_1_out[2]), .pin8(controlled_buffer_1_out[1]), .pin9(controlled_buffer_1_out[0]),
    .pin19(not_16_out), .pin18(n74161_1_pin7), .pin17(n74161_1_pin7), .pin16(n74161_1_pin7),
    .pin15(n74161_1_pin7), .pin14(n74161_1_pin7), .pin13(n74161_1_pin7), .pin12(n74161_1_pin7),
    .pin11(n74161_1_pin7));
  _74273 u_74273_7 (
    .pin2(n74273_7_pin9[3]), .pin3(controlled_buffer_1_out[7]), .pin4(controlled_buffer_1_out[6]),
    .pin5(n74273_7_pin9[2]), .pin6(n74273_7_pin9[1]), .pin7(controlled_buffer_1_out[5]),
    .pin8(controlled_buffer_1_out[4]), .pin9(n74273_7_pin9[0]), .pin19(n74273_7_pin19[0]),
    .pin18(controlled_buffer_1_out[0]), .pin17(controlled_buffer_1_out[1]), .pin16(n74273_7_pin19[1]),
    .pin15(n74273_7_pin19[2]), .pin14(controlled_buffer_1_out[2]), .pin13(controlled_buffer_1_out[3]),
    .pin12(n74273_7_pin19[3]), .pin11(n74273_7_pin11));  // open: pin1
  // RGB_Video #(.cursor("No Cursor"), .height(32), .scale(8), .width(64)) rgb_video_2: pin names not known; wires that end beside it: n74165_1_pin15, n74161_1_pin7, rgb_video_2_p3, rgb_video_1_p2, rom_1_data[15], rgb_video_2_p6, rgb_video_2_p7, controlled_buffer_1_out
  or or_10 (rgb_video_2_p3, or_1_out, rom_1_data[14]);
  TTY #(.cols(64), .rows(12)) tty_1 (
    .data(controlled_buffer_1_out[6:0]), .clk(rgb_video_1_p2), .we(rom_1_data[12]), .clr(or_12_out));
  _74245 u_74245_16 (
    .pin1(n74165_1_pin15), .pin2(controlled_buffer_1_out[0]), .pin3(controlled_buffer_1_out[1]),
    .pin4(controlled_buffer_1_out[2]), .pin5(controlled_buffer_1_out[3]), .pin6(controlled_buffer_1_out[4]),
    .pin7(controlled_buffer_1_out[5]), .pin8(controlled_buffer_1_out[6]), .pin9(controlled_buffer_1_out[7]),
    .pin19(not_20_out), .pin18(n74245_16_pin18), .pin17(n74245_16_pin17), .pin16(n74245_16_pin16),
    .pin15(n74245_16_pin15), .pin14(n74245_16_pin14), .pin13(n74245_16_pin13), .pin12(n74245_16_pin12),
    .pin11(n74245_16_pin11));
  _74245 u_74245_17 (
    .pin1(n74165_1_pin15), .pin2(controlled_buffer_1_out[0]), .pin3(controlled_buffer_1_out[1]),
    .pin4(controlled_buffer_1_out[2]), .pin5(controlled_buffer_1_out[3]), .pin6(controlled_buffer_1_out[4]),
    .pin7(controlled_buffer_1_out[5]), .pin8(controlled_buffer_1_out[6]), .pin9(controlled_buffer_1_out[7]),
    .pin19(not_19_out), .pin18(n74245_17_pin18), .pin17(n74245_17_pin17), .pin16(n74245_17_pin16),
    .pin15(n74245_17_pin15), .pin14(n74245_17_pin14), .pin13(n74245_17_pin13), .pin12(n74245_17_pin12),
    .pin11(n74245_17_pin11));
  _74245 u_74245_18 (
    .pin1(n74165_1_pin15), .pin2(controlled_buffer_1_out[7]), .pin3(controlled_buffer_1_out[6]),
    .pin4(controlled_buffer_1_out[5]), .pin5(controlled_buffer_1_out[4]), .pin6(controlled_buffer_1_out[3]),
    .pin7(controlled_buffer_1_out[2]), .pin8(controlled_buffer_1_out[1]), .pin9(controlled_buffer_1_out[0]),
    .pin19(not_12_out), .pin18(n74245_18_pin18), .pin17(n74245_18_pin17), .pin16(n74245_18_pin16),
    .pin15(n74245_18_pin15), .pin14(n74245_18_pin14), .pin13(n74245_18_pin13), .pin12(n74245_18_pin12),
    .pin11(n74245_18_pin11));
  _74175 u_74175_1 (
    .pin1(n7414_1_pin8), .pin2(n74175_1_pin2), .pin4(controlled_buffer_1_out[3]),
    .pin5(controlled_buffer_1_out[2]), .pin7(n74175_1_pin7), .pin15(n74175_1_pin15),
    .pin13(controlled_buffer_1_out[0]), .pin12(controlled_buffer_1_out[1]), .pin10(n74175_1_pin10),
    .pin9(n74175_1_pin9));  // open: pin3, pin6, pin14, pin11
  Hex_Digit_Display hex_digit_display_1 (.value(n74273_7_pin9));  // open: dp
  _74273 u_74273_8 (
    .pin1(n7414_1_pin8), .pin2(rgb_video_2_p7[0]), .pin3(controlled_buffer_1_out[0]),
    .pin4(controlled_buffer_1_out[1]), .pin5(rgb_video_2_p7[1]), .pin6(rgb_video_2_p7[2]),
    .pin7(controlled_buffer_1_out[2]), .pin8(controlled_buffer_1_out[3]), .pin9(rgb_video_2_p7[3]),
    .pin14(controlled_buffer_1_out[5]), .pin13(controlled_buffer_1_out[4]), .pin12(rgb_video_2_p7[4]),
    .pin11(n74273_8_pin11));  // open: pin19, pin18, pin17, pin16, pin15
  and and_15 (n74273_8_pin11, rgb_video_1_p2, rom_1_data[7]);
  and and_16 (and_16_out, rom_1_data[41], rgb_video_1_p2);
  _74273 u_74273_9 (
    .pin1(n7414_1_pin8), .pin2(n74273_9_pin2), .pin3(n74245_12_pin18), .pin4(n74245_12_pin17),
    .pin5(n74273_9_pin5), .pin6(n74273_9_pin6), .pin7(n74245_12_pin16), .pin8(n74245_12_pin15),
    .pin9(n74273_9_pin9), .pin19(n74273_9_pin19), .pin18(n74245_12_pin11), .pin17(n74245_12_pin12),
    .pin16(n74273_9_pin16), .pin15(n74273_9_pin15), .pin14(n74245_12_pin13), .pin13(n74245_12_pin14),
    .pin12(n74273_9_pin12), .pin11(and_16_out));
  _74273 u_74273_10 (
    .pin1(n7414_1_pin8), .pin2(n74273_10_pin2), .pin3(n74245_13_pin18), .pin4(n74245_13_pin17),
    .pin5(n74273_10_pin5), .pin6(n74273_10_pin6), .pin7(n74245_13_pin16), .pin8(n74245_13_pin15),
    .pin9(n74273_10_pin9), .pin19(n74273_10_pin19), .pin18(n74245_13_pin11), .pin17(n74245_13_pin12),
    .pin16(n74273_10_pin16), .pin15(n74273_10_pin15), .pin14(n74245_13_pin13), .pin13(n74245_13_pin14),
    .pin12(n74273_10_pin12), .pin11(n74273_10_pin11));
  _74193 u_74193_1 (
    .pin1(controlled_buffer_1_out[6]), .pin2(n74245_14_pin4), .pin3(n74245_14_pin5), .pin4(n74193_1_pin4),
    .pin5(n74193_1_pin5), .pin6(n74245_14_pin3), .pin7(n74245_14_pin2), .pin15(controlled_buffer_1_out[7]),
    .pin14(n74193_1_pin14), .pin11(n74193_1_pin11), .pin10(controlled_buffer_1_out[5]),
    .pin9(controlled_buffer_1_out[4]));  // open: pin13, pin12
  Hex_Digit_Display hex_digit_display_2 (.value(n74273_7_pin19));  // open: dp
  Hex_Digit_Display hex_digit_display_3 (.value(n74273_11_pin9));  // open: dp
  and and_17 (and_17_out, rgb_video_1_p2, rom_1_data[6]);
  _74161 u_74161_11 (
    .pin1(n7414_1_pin8), .pin2(rgb_video_1_p2), .pin3(controlled_buffer_1_out[0]),
    .pin4(controlled_buffer_1_out[1]), .pin5(controlled_buffer_1_out[2]), .pin6(controlled_buffer_1_out[3]),
    .pin7(rom_1_data[43]), .pin15(n74161_11_pin15), .pin14(n74245_10_pin18), .pin13(n74245_10_pin17),
    .pin12(n74245_10_pin16), .pin11(n74245_10_pin15), .pin10(n74161_11_pin10), .pin9(n74161_11_pin9));
  _74161 u_74161_12 (
    .pin1(n7414_1_pin8), .pin2(rgb_video_1_p2), .pin3(controlled_buffer_1_out[0]),
    .pin4(controlled_buffer_1_out[1]), .pin5(controlled_buffer_1_out[2]), .pin6(controlled_buffer_1_out[3]),
    .pin7(rom_1_data[43]), .pin15(n74161_12_pin15), .pin14(n74245_11_pin18), .pin13(n74245_11_pin17),
    .pin12(n74245_11_pin16), .pin11(n74245_11_pin15), .pin10(n74161_1_pin7), .pin9(n74161_12_pin9));
  and and_18 (n74273_10_pin11, rgb_video_1_p2, rom_1_data[24]);
  or or_11 (n74193_1_pin14, and_23_out, or_1_out);
  and and_19 (n74175_1_pin9, rgb_video_1_p2, rom_1_data[18]);
  and and_20 (n74273_7_pin11, rgb_video_1_p2, rom_1_data[17]);
  Hex_Digit_Display hex_digit_display_4 (.value(n74273_11_pin19));  // open: dp
  _74273 u_74273_11 (
    .pin2(n74273_11_pin9[3]), .pin3(controlled_buffer_1_out[7]), .pin4(controlled_buffer_1_out[6]),
    .pin5(n74273_11_pin9[2]), .pin6(n74273_11_pin9[1]), .pin7(controlled_buffer_1_out[5]),
    .pin8(controlled_buffer_1_out[4]), .pin9(n74273_11_pin9[0]), .pin19(n74273_11_pin19[0]),
    .pin18(controlled_buffer_1_out[0]), .pin17(controlled_buffer_1_out[1]), .pin16(n74273_11_pin19[1]),
    .pin15(n74273_11_pin19[2]), .pin14(controlled_buffer_1_out[2]), .pin13(controlled_buffer_1_out[3]),
    .pin12(n74273_11_pin19[3]), .pin11(n74273_11_pin11));  // open: pin1
  _74161 u_74161_13 (
    .pin1(n7414_1_pin8), .pin2(rgb_video_1_p2), .pin3(controlled_buffer_1_out[0]),
    .pin4(controlled_buffer_1_out[1]), .pin5(controlled_buffer_1_out[2]), .pin6(controlled_buffer_1_out[3]),
    .pin7(rom_1_data[0]), .pin15(n74161_13_pin15), .pin14(n74245_16_pin18), .pin13(n74245_16_pin17),
    .pin12(n74245_16_pin16), .pin11(n74245_16_pin15), .pin10(n74161_13_pin10), .pin9(n74161_13_pin9));
  _74161 u_74161_14 (
    .pin1(n7414_1_pin8), .pin2(rgb_video_1_p2), .pin3(controlled_buffer_1_out[0]),
    .pin4(controlled_buffer_1_out[1]), .pin5(controlled_buffer_1_out[2]), .pin6(controlled_buffer_1_out[3]),
    .pin7(rom_1_data[0]), .pin15(n74161_14_pin15), .pin14(n74245_17_pin18), .pin13(n74245_17_pin17),
    .pin12(n74245_17_pin16), .pin11(n74245_17_pin15), .pin10(n74161_1_pin7), .pin9(n74161_14_pin9));
  ALU alu_1 (
    .SUB(rom_2_data[0]), .BXR(rom_2_data[2]), .ADD(rom_2_data[1]), .BOR(rom_2_data[3]), .BAN(rom_2_data[4]),
    .BNO(rom_2_data[5]), .ASR(rom_2_data[6]), .LSR(rom_2_data[7]), .LSL(rom_2_data[8]), .B0(n74273_10_pin2),
    .B1(n74273_10_pin5), .B2(n74273_10_pin6), .B3(n74273_10_pin9), .B4(n74273_10_pin12),
    .B5(n74273_10_pin15), .B6(n74273_10_pin16), .B7(n74273_10_pin19), .B8(n74273_14_pin2),
    .B9(n74273_14_pin5), .B10(n74273_14_pin6), .A0(n74273_9_pin2), .B11(n74273_14_pin9), .A1(n74273_9_pin5),
    .A2(n74273_9_pin6), .A3(n74273_9_pin9), .A4(n74273_9_pin12), .A5(n74273_9_pin15), .A6(n74273_9_pin16),
    .A7(n74273_9_pin19), .A8(n74273_13_pin2), .A9(n74273_13_pin5), .A10(n74273_13_pin6),
    .B12(n74273_14_pin12), .A11(n74273_13_pin9), .A12(n74273_13_pin12), .A13(n74273_13_pin15),
    .A14(n74273_13_pin16), .A15(n74273_13_pin19), .B13(n74273_14_pin15), .B14(n74273_14_pin16),
    .B15(n74273_14_pin19), .ZF(alu_1_zf[0]), .CF(alu_1_cf[0]), .S3(n74245_18_pin15), .S2(n74245_18_pin16),
    .S1(n74245_18_pin17), .S0(n74245_18_pin18), .S15(alu_1_s15), .S14(alu_1_s14), .S13(alu_1_s13),
    .S12(alu_1_s12), .S11(alu_1_s11), .S10(alu_1_s10), .S9(alu_1_s9), .S8(alu_1_s8), .S7(n74245_18_pin11),
    .S6(n74245_18_pin12), .S5(n74245_18_pin13), .S4(n74245_18_pin14));
  _74245 u_74245_19 (
    .pin1(n74165_1_pin15), .pin2(controlled_buffer_1_out[7]), .pin3(controlled_buffer_1_out[6]),
    .pin4(controlled_buffer_1_out[5]), .pin5(controlled_buffer_1_out[4]), .pin6(controlled_buffer_1_out[3]),
    .pin7(controlled_buffer_1_out[2]), .pin8(controlled_buffer_1_out[1]), .pin9(controlled_buffer_1_out[0]),
    .pin19(not_14_out), .pin18(alu_1_s8), .pin17(alu_1_s9), .pin16(alu_1_s10), .pin15(alu_1_s11),
    .pin14(alu_1_s12), .pin13(alu_1_s13), .pin12(alu_1_s14), .pin11(alu_1_s15));
  _74161 u_74161_15 (
    .pin1(n7414_1_pin8), .pin2(rgb_video_1_p2), .pin3(controlled_buffer_1_out[4]),
    .pin4(controlled_buffer_1_out[5]), .pin5(controlled_buffer_1_out[6]), .pin6(controlled_buffer_1_out[7]),
    .pin7(rom_1_data[43]), .pin14(n74245_10_pin14), .pin13(n74245_10_pin13), .pin12(n74245_10_pin12),
    .pin11(n74245_10_pin11), .pin10(n74161_11_pin15), .pin9(n74161_11_pin9));  // open: pin15
  _74161 u_74161_16 (
    .pin1(n7414_1_pin8), .pin2(rgb_video_1_p2), .pin3(controlled_buffer_1_out[4]),
    .pin4(controlled_buffer_1_out[5]), .pin5(controlled_buffer_1_out[6]), .pin6(controlled_buffer_1_out[7]),
    .pin7(rom_1_data[43]), .pin15(n74161_11_pin10), .pin14(n74245_11_pin14), .pin13(n74245_11_pin13),
    .pin12(n74245_11_pin12), .pin11(n74245_11_pin11), .pin10(n74161_12_pin15), .pin9(n74161_12_pin9));
  _74245 u_74245_20 (
    .pin1(n74161_1_pin7), .pin2(controlled_buffer_1_out[7]), .pin3(controlled_buffer_1_out[6]),
    .pin4(controlled_buffer_1_out[5]), .pin5(controlled_buffer_1_out[4]), .pin6(controlled_buffer_1_out[3]),
    .pin7(controlled_buffer_1_out[2]), .pin8(controlled_buffer_1_out[1]), .pin9(controlled_buffer_1_out[0]),
    .pin19(n74165_1_pin15), .pin18(n74245_20_pin18), .pin17(n74245_20_pin17), .pin16(n74245_20_pin16),
    .pin15(n74245_20_pin15), .pin14(n74245_20_pin14), .pin13(n74245_20_pin13), .pin12(n74245_20_pin12),
    .pin11(n74245_20_pin11));
  _74245 u_74245_21 (
    .pin1(n74161_1_pin7), .pin2(controlled_buffer_1_out[7]), .pin3(controlled_buffer_1_out[6]),
    .pin4(controlled_buffer_1_out[5]), .pin5(controlled_buffer_1_out[4]), .pin6(controlled_buffer_1_out[3]),
    .pin7(controlled_buffer_1_out[2]), .pin8(controlled_buffer_1_out[1]), .pin9(controlled_buffer_1_out[0]),
    .pin19(n74165_1_pin15), .pin18(n74245_21_pin18), .pin17(n74245_21_pin17), .pin16(n74245_21_pin16),
    .pin15(n74245_21_pin15), .pin14(n74245_21_pin14), .pin13(n74245_21_pin13), .pin12(n74245_21_pin12),
    .pin11(n74245_21_pin11));
  _74193 u_74193_2 (
    .pin1(controlled_buffer_1_out[2]), .pin2(n74245_14_pin8), .pin3(n74245_14_pin9), .pin4(n74193_2_pin4),
    .pin5(n74193_2_pin5), .pin6(n74245_14_pin7), .pin7(n74245_14_pin6), .pin15(controlled_buffer_1_out[3]),
    .pin14(n74193_1_pin14), .pin13(n74193_1_pin4), .pin12(n74193_1_pin5), .pin11(n74193_1_pin11),
    .pin10(controlled_buffer_1_out[1]), .pin9(controlled_buffer_1_out[0]));
  and and_21 (n74273_11_pin11, rgb_video_1_p2, rom_1_data[16]);
  _74273 u_74273_12 (
    .pin1(n7414_1_pin8), .pin2(rgb_video_2_p6[0]), .pin3(controlled_buffer_1_out[0]),
    .pin4(controlled_buffer_1_out[1]), .pin5(rgb_video_2_p6[1]), .pin6(rgb_video_2_p6[2]),
    .pin7(controlled_buffer_1_out[2]), .pin8(controlled_buffer_1_out[3]), .pin9(rgb_video_2_p6[3]),
    .pin15(rgb_video_2_p6[5]), .pin14(controlled_buffer_1_out[5]), .pin13(controlled_buffer_1_out[4]),
    .pin12(rgb_video_2_p6[4]), .pin11(and_17_out));  // open: pin19, pin18, pin17, pin16
  or or_12 (or_12_out, ~n7414_1_pin8, rom_1_data[13]);  // OR_Gate
  _74161 u_74161_17 (
    .pin1(n7414_1_pin8), .pin2(rgb_video_1_p2), .pin3(controlled_buffer_1_out[4]),
    .pin4(controlled_buffer_1_out[5]), .pin5(controlled_buffer_1_out[6]), .pin6(controlled_buffer_1_out[7]),
    .pin7(rom_1_data[0]), .pin14(n74245_16_pin14), .pin13(n74245_16_pin13), .pin12(n74245_16_pin12),
    .pin11(n74245_16_pin11), .pin10(n74161_13_pin15), .pin9(n74161_13_pin9));  // open: pin15
  _74161 u_74161_18 (
    .pin1(n7414_1_pin8), .pin2(rgb_video_1_p2), .pin3(controlled_buffer_1_out[4]),
    .pin4(controlled_buffer_1_out[5]), .pin5(controlled_buffer_1_out[6]), .pin6(controlled_buffer_1_out[7]),
    .pin7(rom_1_data[0]), .pin15(n74161_13_pin10), .pin14(n74245_17_pin14), .pin13(n74245_17_pin13),
    .pin12(n74245_17_pin12), .pin11(n74245_17_pin11), .pin10(n74161_14_pin15), .pin9(n74161_14_pin9));
  ROM #(.addrWidth(4), .dataWidth(9)) rom_2 (.addr(rom_1_data[31:28]), .data(rom_2_data));
  _74273 u_74273_13 (
    .pin1(n7414_1_pin8), .pin2(n74273_13_pin2), .pin3(n74245_20_pin18), .pin4(n74245_20_pin17),
    .pin5(n74273_13_pin5), .pin6(n74273_13_pin6), .pin7(n74245_20_pin16), .pin8(n74245_20_pin15),
    .pin9(n74273_13_pin9), .pin19(n74273_13_pin19), .pin18(n74245_20_pin11), .pin17(n74245_20_pin12),
    .pin16(n74273_13_pin16), .pin15(n74273_13_pin15), .pin14(n74245_20_pin13), .pin13(n74245_20_pin14),
    .pin12(n74273_13_pin12), .pin11(n74273_13_pin11));
  _74273 u_74273_14 (
    .pin1(n7414_1_pin8), .pin2(n74273_14_pin2), .pin3(n74245_21_pin18), .pin4(n74245_21_pin17),
    .pin5(n74273_14_pin5), .pin6(n74273_14_pin6), .pin7(n74245_21_pin16), .pin8(n74245_21_pin15),
    .pin9(n74273_14_pin9), .pin19(n74273_14_pin19), .pin18(n74245_21_pin11), .pin17(n74245_21_pin12),
    .pin16(n74273_14_pin16), .pin15(n74273_14_pin15), .pin14(n74245_21_pin13), .pin13(n74245_21_pin14),
    .pin12(n74273_14_pin12), .pin11(n74273_14_pin11));
  not not_23 (n74193_1_pin11, rom_1_data[22]);
  and and_22 (n74273_13_pin11, rom_1_data[42], rgb_video_1_p2);
  and and_23 (and_23_out, n74245_14_pin7, n74245_14_pin9, n74245_14_pin8, n74245_14_pin2, n74245_14_pin3, n74245_14_pin5, n74245_14_pin4);
  not not_24 (n74161_13_pin9, rom_1_data[8]);
  not not_25 (n74161_14_pin9, rom_1_data[9]);
  and and_24 (and_24_out, rgb_video_1_p2, rom_1_data[40]);
  or or_13 (or_13_out, rom_1_data[53], and_24_out);
  _74273 u_74273_15 (
    .pin1(n74161_1_pin7), .pin2(n74273_15_pin2), .pin3(n74273_15_pin3), .pin4(n74273_15_pin4),
    .pin5(n74273_15_pin5), .pin11(or_13_out));  // open: pin6, pin7, pin8, pin9, pin19, pin18, pin17, pin16, pin15, pin14, pin13, pin12
  and and_25 (n74273_14_pin11, rgb_video_1_p2, rom_1_data[25]);
  nand nand_1 (n74193_2_pin5, rgb_video_1_p2, rom_1_data[21]);
  nand nand_2 (n74193_2_pin4, rom_1_data[20], rgb_video_1_p2);
  BitSelector #(.width(2)) bitselector_1 (.in(alu_1_cf), .out(n74273_15_pin3), .sel(and_26_out));
  BitSelector #(.width(2)) bitselector_2 (.in(alu_1_zf), .out(n74273_15_pin4), .sel(and_26_out));
  D_Flip_Flop d_ff_1 (.D(n74273_15_pin5), .clk(rom_1_data[60]), .Q(alu_1_zf[1]), .reset(undriven));  // open: Qn, preset
  D_Flip_Flop d_ff_2 (.D(n74273_15_pin2), .clk(rom_1_data[60]), .Q(alu_1_cf[1]), .preset(undriven));  // open: Qn, reset
  and and_26 (and_26_out, rgb_video_1_p2, rom_1_data[53]);
  _74245 u_74245_22 (
    .pin1(n74161_1_pin7), .pin2(n74273_13_pin2), .pin3(n74273_13_pin5), .pin4(n74273_13_pin6),
    .pin5(n74273_13_pin9), .pin6(n74273_13_pin12), .pin7(n74273_13_pin15), .pin8(n74273_13_pin16),
    .pin9(n74273_13_pin19), .pin19(not_10_out), .pin18(controlled_buffer_1_out[7]),
    .pin17(controlled_buffer_1_out[6]), .pin16(controlled_buffer_1_out[5]),
    .pin15(controlled_buffer_1_out[4]), .pin14(controlled_buffer_1_out[3]),
    .pin13(controlled_buffer_1_out[2]), .pin12(controlled_buffer_1_out[1]), .pin11(controlled_buffer_1_out[0]));
  _74245 u_74245_23 (
    .pin1(n74161_1_pin7), .pin2(n74273_9_pin2), .pin3(n74273_9_pin5), .pin4(n74273_9_pin6),
    .pin5(n74273_9_pin9), .pin6(n74273_9_pin12), .pin7(n74273_9_pin15), .pin8(n74273_9_pin16),
    .pin9(n74273_9_pin19), .pin19(not_11_out), .pin18(controlled_buffer_1_out[7]),
    .pin17(controlled_buffer_1_out[6]), .pin16(controlled_buffer_1_out[5]),
    .pin15(controlled_buffer_1_out[4]), .pin14(controlled_buffer_1_out[3]),
    .pin13(controlled_buffer_1_out[2]), .pin12(controlled_buffer_1_out[1]), .pin11(controlled_buffer_1_out[0]));
  nor nor_4 (n74161_12_pin9, and_27_out, and_28_out, and_29_out, rom_1_data[36]);
  and and_27 (and_27_out, n74273_15_pin5, rom_1_data[34]);
  and and_28 (and_28_out, rom_1_data[35], n74273_15_pin2);
  LED AL0 (.in(rom_1_data[31]));
  LED INH (.in(rom_1_data[63]));
  and and_29 (and_29_out, rom_1_data[3], not_2_out);
  LED AL1 (.in(rom_1_data[30]));
  LED AL2 (.in(rom_1_data[29]));
  LED SCR (.in(rom_1_data[62]));
  LED KBO (.in(rom_1_data[61]));
  nor nor_5 (n74161_11_pin9, and_30_out, and_31_out, and_32_out, rom_1_data[39]);
  and and_30 (and_30_out, n74273_15_pin5, rom_1_data[37]);
  and and_31 (and_31_out, rom_1_data[38], n74273_15_pin2);
  and and_32 (and_32_out, rom_1_data[2], not_2_out);
  LED AL3 (.in(rom_1_data[28]));
  LED EBO (.in(rom_1_data[27]));
  LED ELO (.in(rom_1_data[26]));
  LED KRE (.in(rom_1_data[60]));
  LED GRI (.in(rom_1_data[59]));
  LED GCE (.in(rom_1_data[58]));
  LED BLI (.in(rom_1_data[25]));
  LED BBI (.in(rom_1_data[24]));
  LED SPO (.in(rom_1_data[23]));
  LED GCR (.in(rom_1_data[57]));
  LED GBE (.in(rom_1_data[56]));
  LED GDI (.in(rom_1_data[55]));
  LED SPI (.in(rom_1_data[22]));
  LED ISP (.in(rom_1_data[21]));
  LED GRF (.in(rom_1_data[54]));
  LED IE (.in(rom_1_data[53]));
  LED DSP (.in(rom_1_data[20]));
  LED FFO (.in(rom_1_data[19]));
  LED HPI (.in(rom_1_data[18]));
  LED IRI (.in(rom_1_data[52]));
  LED OBI (.in(rom_1_data[51]));
  LED OLI (.in(rom_1_data[50]));
  LED HBI (.in(rom_1_data[17]));
  LED HLI (.in(rom_1_data[16]));
  LED CW (.in(rom_1_data[15]));
  LED RO (.in(rom_1_data[49]));
  LED RI (.in(rom_1_data[48]));
  LED MBI (.in(rom_1_data[47]));
  LED CC (.in(rom_1_data[14]));
  LED CT (.in(rom_1_data[13]));
  LED MLI (.in(rom_1_data[46]));
  LED CBO (.in(rom_1_data[45]));
  LED TW (.in(rom_1_data[12]));
  LED XLO (.in(rom_1_data[11]));
  LED XBO (.in(rom_1_data[10]));
  LED CLO (.in(rom_1_data[44]));
  LED CE (.in(rom_1_data[43]));
  LED ALI (.in(rom_1_data[42]));
  LED XLI (.in(rom_1_data[9]));
  LED XBI (.in(rom_1_data[8]));
  LED CYI (.in(rom_1_data[7]));
  LED ABI (.in(rom_1_data[41]));
  LED FI (.in(rom_1_data[40]));
  LED JB (.in(rom_1_data[39]));
  LED CXI (.in(rom_1_data[6]));
  LED OBO (.in(rom_1_data[5]));
  LED JCB (.in(rom_1_data[38]));
  LED JZB (.in(rom_1_data[37]));
  LED OLO (.in(rom_1_data[4]));
  LED JVL (.in(rom_1_data[3]));
  LED JVB (.in(rom_1_data[2]));
  LED JL (.in(rom_1_data[36]));
  LED JCL (.in(rom_1_data[35]));
  LED JZL (.in(rom_1_data[34]));
  LED HLT (.in(rom_1_data[1]));
  LED INX (.in(rom_1_data[0]));
  LED ALO (.in(rom_1_data[33]));
  LED ABO (.in(rom_1_data[32]));
  // also tied to GND on the sheet: n74165_1_pin15
  // also tied to VCC on the sheet: n74161_1_pin7

  // Notes on the sheet:
  //   contents of rom_1 (hex, n*v repeats v):
  //   a00000000000 500000000000 12000000000000 8000080000000000 c000000000000000 16*0 c000000000000000
  //   10*0 a00000000000 500000000000 12000000000000 8000080000000000 8000a00000000000 8000500000000000
  //   80020c0000000000 8000a00000000000 8000500000000000 80020a0000000000 c000000000000000 21*0
  //   a00000000000 500000000000 12000000000000 8000080000000000 8000a00000000000 8000500000000000
  //   80020a0000000000 c000000000000000 24*0 a00000000000 500000000000 12000000000000 8000080000000000
  //   8000a00000000000 8000500000000000 80020c0000000000 c000000000000000 24*0 a00000000000 500000000000
  //   12000000000000 8000080000000000 8000a00000000000 8000500000000000 8002080000000200 8000a00000000000
  //   8000500000000000 8002880000000100 8000400000000800 8002040000000001 8000800000000400
  //   8000400000000800 8002020000000000 c000000000000000 16*0 a00000000000 500000000000 12000000000000
  //   8000080000000000 8000a00000000000 8000500000000000 8006080000000000 8000a00000000000
  //   8000500000000000 8002880000000000 8000400000000010 8002020000000000 c000000000000000 19*0
  //   a00000000000 500000000000 12000000000000 8000080000000000 8000a00000000000 8000500000000000
  //   8006080000000000 8000a00000000000 8000500000000000 8002880000000000 8000400000000010
  //   8002040000000000 c000000000000000 19*0 a00000000000 500000000000 12000000000000 8000080000000000
  //   8000a00000000000 8000500000000000 8002080000000200 8000a00000000000 8000500000000000
  //   8002880000000100 8000400000000800 8001000200000001 8000800000000400 8000400000000800
  //   8001000100000000 c000000000000000 16*0 a00000000000 500000000000 12000000000000 8000080000000000
  //   8000a00000000000 8000500000000000 8006080000000000 8000a00000000000 8000500000000000
  //   8002880000000000 8000400000000010 8001000100000000 c000000000000000 19*0 a00000000000 500000000000
  //   12000000000000 8000080000000000 8000a00000000000 8000500000000000 8006080000000000 8000a00000000000
  //   8000500000000000 8002880000000000 8000400000000010 8001000200000000 c000000000000000 19*0
  //   a00000000000 500000000000 12000000000000 8000080000000000 8000a00000000000 8000500000000000
  //   8002080000000200 8000a00000000000 8000500000000000 8002880000000100 8000400000000800
  //   8002000002000001 8000800000000400 8000400000000800 8002000001000000 8004000014000000
  //   8000030018000000 8000040000000010 c000000000000000 13*0 a00000000000 500000000000 12000000000000
  //   8000080000000000 8000a00000000000 8000500000000000 8002080000000200 8000a00000000000
  //   8000500000000000 8002880000000100 8000400000000800 8002000002000001 8000800000000400
  //   8000400000000800 8002000001000000 8004000024000000 8000030028000000 8000040000000010
  //   c000000000000000 13*0 a00000000000 500000000000 12000000000000 8000080000000000 8000a00000000000
  //   8000500000000000 8002080000000200 8000a00000000000 8000500000000000 8002880000000100
  //   8000400000000800 8002000002000001 8000800000000400 8000400000000800 8002000001000000
  //   8004000034000000 8000020038000000 8000040000000010 c000000000000000 13*0 a00000000000 500000000000
  //   12000000000000 8000080000000000 8000a00000000000 8000500000000000 8002080000000200 8000a00000000000
  //   8000500000000000 8002880000000100 8000400000000800 8002000002000001 8000800000000400
  //   8000400000000800 8002000001000000 8004000044000000 8000020048000000 8000040000000010
  //   c000000000000000 13*0 a00000000000 500000000000 12000000000000 8000080000000000 8000a00000000000
  //   8000500000000000 8002080000000200 8000a00000000000 8000500000000000 8002880000000100
  //   8000400000000800 8002000002000001 8000800000000400 8000400000000800 8002000001000000
  //   8004000054000000 8000020058000000 8000040000000010 c000000000000000 13*0 a00000000000 500000000000
  //   12000000000000 8000080000000000 8004010064000000 8000020068000000 8000040000000010 c000000000000000
  //   24*0 a00000000000 500000000000 12000000000000 8000080000000000 8000a00000000000 8000500000000000
  //   8002080000000200 8000a00000000000 8000500000000000 8002880000000100 8000400000000800
  //   8002000002000001 8000800000000400 8000400000000800 8002000001000000 8004000074000000
  //   8000020078000000 8000040000000010 c000000000000000 13*0 a00000000000 5000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
  //   contents of rom_2 (hex, n*v repeats v):
  //   0 1 2 4 8 10 20 40 80 100
endmodule

module ALU (
  input  A1,
  input  A3,
  input  A5,
  input  A7,
  input  A9,
  input  A11,
  input  A13,
  input  A15,
  input  A0,
  input  A2,
  input  A4,
  input  A6,
  input  A8,
  input  A10,
  input  A12,
  input  A14,
  input  B1,
  input  B3,
  input  B5,
  input  B7,
  input  B9,
  input  B11,
  input  B13,
  input  B15,
  input  B0,
  input  B2,
  input  B4,
  input  B6,
  input  B8,
  input  B10,
  input  B12,
  input  B14,
  input  SUB,
  input  BXR,
  input  ADD,
  input  BOR,
  input  BAN,
  input  BNO,
  input  ASR,
  input  LSR,
  input  LSL,
  output CF,
  output S15,
  output S14,
  output S13,
  output S12,
  output S11,
  output S10,
  output S9,
  output S8,
  output S7,
  output S6,
  output S5,
  output S4,
  output S3,
  output S2,
  output S1,
  output S0,
  output ZF
);

  wire and_2_out, and_3_out, and_4_out, and_5_out, and_6_out, and_7_out, and_8_out, and_9_out, and_10_out,
       and_11_out, and_12_out, and_13_out, and_14_out, and_15_out, and_16_out, and_17_out, n7486_2_pin3,
       n7486_2_pin6, n7486_2_pin8, n7486_2_pin11, n7486_3_pin3, n7486_3_pin6, n7486_3_pin8, n7486_3_pin11,
       n7486_4_pin3, n7486_4_pin6, n7486_4_pin8, n7486_4_pin11, n74245_1_pin1, n74283_1_pin1, n74283_1_pin4,
       n74283_1_pin9, n74283_1_pin10, n74283_1_pin13, n74283_2_pin1, n74283_2_pin4, n74283_2_pin9,
       n74283_2_pin10, n74283_2_pin13, n74283_3_pin1, n74283_3_pin4, n74283_3_pin9, n74283_3_pin10,
       n74283_3_pin13, n74283_4_pin1, n74283_4_pin4, n74283_4_pin10, n74283_4_pin13, nor_1_out, not_1_out,
       not_2_out, not_3_out, not_4_out, not_5_out, not_6_out, not_7_out, not_8_out, not_9_out, not_10_out,
       not_11_out, not_12_out, not_13_out, not_14_out, not_15_out, not_16_out, not_17_out, not_18_out,
       not_19_out, not_20_out, not_21_out, not_22_out, not_23_out, or_1_out, or_2_out, or_3_out, or_4_out,
       or_5_out, or_6_out, or_7_out, or_8_out, or_9_out, or_10_out, or_11_out, or_12_out, or_13_out,
       or_14_out, or_15_out, or_16_out, xor_1_out, xor_2_out, xor_3_out, xor_4_out, xor_5_out, xor_6_out,
       xor_7_out, xor_8_out, xor_9_out, xor_10_out, xor_11_out, xor_12_out, xor_13_out, xor_14_out,
       xor_15_out, xor_16_out;
  wire [3:0] n7486_1_pin11;
  wire [15:0] shifter_1_out, shifter_2_out, shifter_3_out;

  not not_1 (not_1_out, BOR);
  not not_2 (not_2_out, BAN);
  not not_3 (not_3_out, BNO);
  not not_4 (not_4_out, ASR);
  not not_5 (not_5_out, LSR);
  not not_6 (not_6_out, LSL);
  not not_7 (not_7_out, BXR);
  nor nor_1 (nor_1_out, SUB, ADD);
  _7486 u_7486_1 (
    .pin1(SUB), .pin2(B12), .pin3(n7486_1_pin11[3]), .pin4(SUB), .pin5(B13), .pin6(n7486_1_pin11[2]),
    .pin13(SUB), .pin12(B15), .pin11(n7486_1_pin11[0]), .pin10(SUB), .pin9(B14), .pin8(n7486_1_pin11[1]));
  _7486 u_7486_2 (
    .pin1(SUB), .pin2(B8), .pin3(n7486_2_pin3), .pin4(SUB), .pin5(B9), .pin6(n7486_2_pin6), .pin13(SUB),
    .pin12(B11), .pin11(n7486_2_pin11), .pin10(SUB), .pin9(B10), .pin8(n7486_2_pin8));
  _7486 u_7486_3 (
    .pin1(SUB), .pin2(B4), .pin3(n7486_3_pin3), .pin4(SUB), .pin5(B5), .pin6(n7486_3_pin6), .pin13(SUB),
    .pin12(B7), .pin11(n7486_3_pin11), .pin10(SUB), .pin9(B6), .pin8(n7486_3_pin8));
  _7486 u_7486_4 (
    .pin1(SUB), .pin2(B0), .pin3(n7486_4_pin3), .pin4(SUB), .pin5(B1), .pin6(n7486_4_pin6), .pin13(SUB),
    .pin12(B3), .pin11(n7486_4_pin11), .pin10(SUB), .pin9(B2), .pin8(n7486_4_pin8));
  and and_1 (ZF, ~n74283_1_pin4, ~n74283_1_pin1, ~n74283_1_pin13, ~n74283_1_pin10, ~n74283_2_pin4, ~n74283_2_pin1, ~n74283_2_pin13, ~n74283_2_pin10, ~n74283_3_pin4, ~n74283_3_pin1, ~n74283_3_pin13, ~n74283_3_pin10, ~n74283_4_pin4, ~n74283_4_pin1, ~n74283_4_pin13, ~n74283_4_pin10);  // AND_Gate
  _74283 u_74283_1 (
    .pin1(n74283_1_pin1), .pin2(n7486_1_pin11[1]), .pin3(A14), .pin4(n74283_1_pin4), .pin5(A15),
    .pin6(n7486_1_pin11[0]), .pin7(SUB), .pin15(n7486_1_pin11[2]), .pin14(A13), .pin13(n74283_1_pin13),
    .pin12(A12), .pin11(n7486_1_pin11[3]), .pin10(n74283_1_pin10), .pin9(n74283_1_pin9));
  _74283 u_74283_2 (
    .pin1(n74283_2_pin1), .pin2(n7486_2_pin8), .pin3(A10), .pin4(n74283_2_pin4), .pin5(A11),
    .pin6(n7486_2_pin11), .pin7(n74283_1_pin9), .pin15(n7486_2_pin6), .pin14(A9), .pin13(n74283_2_pin13),
    .pin12(A8), .pin11(n7486_2_pin3), .pin10(n74283_2_pin10), .pin9(n74283_2_pin9));
  _74283 u_74283_3 (
    .pin1(n74283_3_pin1), .pin2(n7486_3_pin8), .pin3(A6), .pin4(n74283_3_pin4), .pin5(A7),
    .pin6(n7486_3_pin11), .pin7(n74283_2_pin9), .pin15(n7486_3_pin6), .pin14(A5), .pin13(n74283_3_pin13),
    .pin12(A4), .pin11(n7486_3_pin3), .pin10(n74283_3_pin10), .pin9(n74283_3_pin9));
  _74283 u_74283_4 (
    .pin1(n74283_4_pin1), .pin2(n7486_4_pin8), .pin3(A2), .pin4(n74283_4_pin4), .pin5(A3),
    .pin6(n7486_4_pin11), .pin7(n74283_3_pin9), .pin15(n7486_4_pin6), .pin14(A1), .pin13(n74283_4_pin13),
    .pin12(A0), .pin11(n7486_4_pin3), .pin10(n74283_4_pin10), .pin9(CF));
  Shifter #(.width(16)) shifter_1 (
    .in({A0, A1, A2, A3, A4, A5, A6, A7, A8, A9, A10, A11, A12, A13, A14, A15}), .\dist (n7486_1_pin11),
    .out(shifter_1_out));
  Shifter #(.shift("lr"), .width(16)) shifter_2 (
    .in({A0, A1, A2, A3, A4, A5, A6, A7, A8, A9, A10, A11, A12, A13, A14, A15}), .\dist (n7486_1_pin11),
    .out(shifter_2_out));
  Shifter #(.shift("ar"), .width(16)) shifter_3 (
    .in({A0, A1, A2, A3, A4, A5, A6, A7, A8, A9, A10, A11, A12, A13, A14, A15}), .\dist (n7486_1_pin11),
    .out(shifter_3_out));
  not not_8 (not_8_out, A15);
  not not_9 (not_9_out, A14);
  not not_10 (not_10_out, A13);
  not not_11 (not_11_out, A12);
  not not_12 (not_12_out, A11);
  not not_13 (not_13_out, A10);
  not not_14 (not_14_out, A9);
  not not_15 (not_15_out, A8);
  not not_16 (not_16_out, A7);
  not not_17 (not_17_out, A6);
  not not_18 (not_18_out, A5);
  not not_19 (not_19_out, A4);
  not not_20 (not_20_out, A3);
  not not_21 (not_21_out, A2);
  not not_22 (not_22_out, A1);
  not not_23 (not_23_out, A0);
  and and_2 (and_2_out, n7486_1_pin11[0], A15);
  and and_3 (and_3_out, n7486_1_pin11[1], A14);
  and and_4 (and_4_out, n7486_1_pin11[2], A13);
  and and_5 (and_5_out, n7486_1_pin11[3], A12);
  and and_6 (and_6_out, n7486_2_pin11, A11);
  and and_7 (and_7_out, n7486_2_pin8, A10);
  and and_8 (and_8_out, n7486_2_pin6, A9);
  and and_9 (and_9_out, n7486_2_pin3, A8);
  and and_10 (and_10_out, n7486_3_pin11, A7);
  and and_11 (and_11_out, n7486_3_pin8, A6);
  and and_12 (and_12_out, n7486_3_pin6, A5);
  and and_13 (and_13_out, n7486_3_pin3, A4);
  and and_14 (and_14_out, n7486_4_pin11, A3);
  and and_15 (and_15_out, n7486_4_pin8, A2);
  and and_16 (and_16_out, n7486_4_pin6, A1);
  and and_17 (and_17_out, n7486_4_pin3, A0);
  or or_1 (or_1_out, n7486_1_pin11[0], A15);
  or or_2 (or_2_out, n7486_1_pin11[1], A14);
  or or_3 (or_3_out, n7486_1_pin11[2], A13);
  or or_4 (or_4_out, n7486_1_pin11[3], A12);
  or or_5 (or_5_out, n7486_2_pin11, A11);
  or or_6 (or_6_out, n7486_2_pin8, A10);
  or or_7 (or_7_out, n7486_2_pin6, A9);
  or or_8 (or_8_out, n7486_2_pin3, A8);
  or or_9 (or_9_out, n7486_3_pin11, A7);
  or or_10 (or_10_out, n7486_3_pin8, A6);
  or or_11 (or_11_out, n7486_3_pin6, A5);
  or or_12 (or_12_out, n7486_3_pin3, A4);
  or or_13 (or_13_out, n7486_4_pin11, A3);
  or or_14 (or_14_out, n7486_4_pin8, A2);
  or or_15 (or_15_out, n7486_4_pin6, A1);
  or or_16 (or_16_out, n7486_4_pin3, A0);
  xor xor_1 (xor_1_out, n7486_1_pin11[0], A15);
  xor xor_2 (xor_2_out, n7486_1_pin11[1], A14);
  xor xor_3 (xor_3_out, n7486_1_pin11[2], A13);
  xor xor_4 (xor_4_out, n7486_1_pin11[3], A12);
  xor xor_5 (xor_5_out, n7486_2_pin11, A11);
  xor xor_6 (xor_6_out, n7486_2_pin8, A10);
  xor xor_7 (xor_7_out, n7486_2_pin6, A9);
  xor xor_8 (xor_8_out, n7486_2_pin3, A8);
  xor xor_9 (xor_9_out, n7486_3_pin11, A7);
  xor xor_10 (xor_10_out, n7486_3_pin8, A6);
  xor xor_11 (xor_11_out, n7486_3_pin6, A5);
  xor xor_12 (xor_12_out, n7486_3_pin3, A4);
  xor xor_13 (xor_13_out, n7486_4_pin11, A3);
  xor xor_14 (xor_14_out, n7486_4_pin8, A2);
  xor xor_15 (xor_15_out, n7486_4_pin6, A1);
  xor xor_16 (xor_16_out, n7486_4_pin3, A0);
  _74245 u_74245_1 (
    .pin1(n74245_1_pin1), .pin2(S7), .pin3(S6), .pin4(S5), .pin5(S4), .pin6(S3), .pin7(S2), .pin8(S1),
    .pin9(S0), .pin19(not_7_out), .pin18(xor_9_out), .pin17(xor_10_out), .pin16(xor_11_out),
    .pin15(xor_12_out), .pin14(xor_13_out), .pin13(xor_14_out), .pin12(xor_15_out), .pin11(xor_16_out));
  _74245 u_74245_2 (
    .pin1(n74245_1_pin1), .pin2(S15), .pin3(S14), .pin4(S13), .pin5(S12), .pin6(S11), .pin7(S10), .pin8(S9),
    .pin9(S8), .pin19(not_7_out), .pin18(xor_1_out), .pin17(xor_2_out), .pin16(xor_3_out), .pin15(xor_4_out),
    .pin14(xor_5_out), .pin13(xor_6_out), .pin12(xor_7_out), .pin11(xor_8_out));
  _74245 u_74245_3 (
    .pin1(n74245_1_pin1), .pin2(S7), .pin3(S6), .pin4(S5), .pin5(S4), .pin6(S3), .pin7(S2), .pin8(S1),
    .pin9(S0), .pin19(not_1_out), .pin18(or_9_out), .pin17(or_10_out), .pin16(or_11_out), .pin15(or_12_out),
    .pin14(or_13_out), .pin13(or_14_out), .pin12(or_15_out), .pin11(or_16_out));
  _74245 u_74245_4 (
    .pin1(n74245_1_pin1), .pin2(S15), .pin3(S14), .pin4(S13), .pin5(S12), .pin6(S11), .pin7(S10), .pin8(S9),
    .pin9(S8), .pin19(not_1_out), .pin18(or_1_out), .pin17(or_2_out), .pin16(or_3_out), .pin15(or_4_out),
    .pin14(or_5_out), .pin13(or_6_out), .pin12(or_7_out), .pin11(or_8_out));
  _74245 u_74245_5 (
    .pin1(n74245_1_pin1), .pin2(S7), .pin3(S6), .pin4(S5), .pin5(S4), .pin6(S3), .pin7(S2), .pin8(S1),
    .pin9(S0), .pin19(not_2_out), .pin18(and_10_out), .pin17(and_11_out), .pin16(and_12_out),
    .pin15(and_13_out), .pin14(and_14_out), .pin13(and_15_out), .pin12(and_16_out), .pin11(and_17_out));
  _74245 u_74245_6 (
    .pin1(n74245_1_pin1), .pin2(S15), .pin3(S14), .pin4(S13), .pin5(S12), .pin6(S11), .pin7(S10), .pin8(S9),
    .pin9(S8), .pin19(not_2_out), .pin18(and_2_out), .pin17(and_3_out), .pin16(and_4_out), .pin15(and_5_out),
    .pin14(and_6_out), .pin13(and_7_out), .pin12(and_8_out), .pin11(and_9_out));
  _74245 u_74245_7 (
    .pin1(n74245_1_pin1), .pin2(S7), .pin3(S6), .pin4(S5), .pin5(S4), .pin6(S3), .pin7(S2), .pin8(S1),
    .pin9(S0), .pin19(not_3_out), .pin18(not_16_out), .pin17(not_17_out), .pin16(not_18_out),
    .pin15(not_19_out), .pin14(not_20_out), .pin13(not_21_out), .pin12(not_22_out), .pin11(not_23_out));
  _74245 u_74245_8 (
    .pin1(n74245_1_pin1), .pin2(S15), .pin3(S14), .pin4(S13), .pin5(S12), .pin6(S11), .pin7(S10), .pin8(S9),
    .pin9(S8), .pin19(not_3_out), .pin18(not_8_out), .pin17(not_9_out), .pin16(not_10_out),
    .pin15(not_11_out), .pin14(not_12_out), .pin13(not_13_out), .pin12(not_14_out), .pin11(not_15_out));
  _74245 u_74245_9 (
    .pin1(n74245_1_pin1), .pin2(S7), .pin3(S6), .pin4(S5), .pin5(S4), .pin6(S3), .pin7(S2), .pin8(S1),
    .pin9(S0), .pin19(not_4_out), .pin18(shifter_3_out[8]), .pin17(shifter_3_out[9]),
    .pin16(shifter_3_out[10]), .pin15(shifter_3_out[11]), .pin14(shifter_3_out[12]),
    .pin13(shifter_3_out[13]), .pin12(shifter_3_out[14]), .pin11(shifter_3_out[15]));
  _74245 u_74245_10 (
    .pin1(n74245_1_pin1), .pin2(S15), .pin3(S14), .pin4(S13), .pin5(S12), .pin6(S11), .pin7(S10), .pin8(S9),
    .pin9(S8), .pin19(not_4_out), .pin18(shifter_3_out[0]), .pin17(shifter_3_out[1]),
    .pin16(shifter_3_out[2]), .pin15(shifter_3_out[3]), .pin14(shifter_3_out[4]), .pin13(shifter_3_out[5]),
    .pin12(shifter_3_out[6]), .pin11(shifter_3_out[7]));
  _74245 u_74245_11 (
    .pin1(n74245_1_pin1), .pin2(S7), .pin3(S6), .pin4(S5), .pin5(S4), .pin6(S3), .pin7(S2), .pin8(S1),
    .pin9(S0), .pin19(not_5_out), .pin18(shifter_2_out[8]), .pin17(shifter_2_out[9]),
    .pin16(shifter_2_out[10]), .pin15(shifter_2_out[11]), .pin14(shifter_2_out[12]),
    .pin13(shifter_2_out[13]), .pin12(shifter_2_out[14]), .pin11(shifter_2_out[15]));
  _74245 u_74245_12 (
    .pin1(n74245_1_pin1), .pin2(S15), .pin3(S14), .pin4(S13), .pin5(S12), .pin6(S11), .pin7(S10), .pin8(S9),
    .pin9(S8), .pin19(not_5_out), .pin18(shifter_2_out[0]), .pin17(shifter_2_out[1]),
    .pin16(shifter_2_out[2]), .pin15(shifter_2_out[3]), .pin14(shifter_2_out[4]), .pin13(shifter_2_out[5]),
    .pin12(shifter_2_out[6]), .pin11(shifter_2_out[7]));
  _74245 u_74245_13 (
    .pin1(n74245_1_pin1), .pin2(S7), .pin3(S6), .pin4(S5), .pin5(S4), .pin6(S3), .pin7(S2), .pin8(S1),
    .pin9(S0), .pin19(not_6_out), .pin18(shifter_1_out[8]), .pin17(shifter_1_out[9]),
    .pin16(shifter_1_out[10]), .pin15(shifter_1_out[11]), .pin14(shifter_1_out[12]),
    .pin13(shifter_1_out[13]), .pin12(shifter_1_out[14]), .pin11(shifter_1_out[15]));
  _74245 u_74245_14 (
    .pin1(n74245_1_pin1), .pin2(S15), .pin3(S14), .pin4(S13), .pin5(S12), .pin6(S11), .pin7(S10), .pin8(S9),
    .pin9(S8), .pin19(not_6_out), .pin18(shifter_1_out[0]), .pin17(shifter_1_out[1]),
    .pin16(shifter_1_out[2]), .pin15(shifter_1_out[3]), .pin14(shifter_1_out[4]), .pin13(shifter_1_out[5]),
    .pin12(shifter_1_out[6]), .pin11(shifter_1_out[7]));
  _74245 u_74245_15 (
    .pin1(n74245_1_pin1), .pin2(S7), .pin3(S6), .pin4(S5), .pin5(S4), .pin6(S3), .pin7(S2), .pin8(S1),
    .pin9(S0), .pin19(nor_1_out), .pin18(n74283_3_pin4), .pin17(n74283_3_pin1), .pin16(n74283_3_pin13),
    .pin15(n74283_3_pin10), .pin14(n74283_4_pin4), .pin13(n74283_4_pin1), .pin12(n74283_4_pin13),
    .pin11(n74283_4_pin10));
  _74245 u_74245_16 (
    .pin1(n74245_1_pin1), .pin2(S15), .pin3(S14), .pin4(S13), .pin5(S12), .pin6(S11), .pin7(S10), .pin8(S9),
    .pin9(S8), .pin19(nor_1_out), .pin18(n74283_1_pin4), .pin17(n74283_1_pin1), .pin16(n74283_1_pin13),
    .pin15(n74283_1_pin10), .pin14(n74283_2_pin4), .pin13(n74283_2_pin1), .pin12(n74283_2_pin13),
    .pin11(n74283_2_pin10));
  // also tied to GND on the sheet: n74245_1_pin1

  // Notes on the sheet:
  //   1
  //   1
endmodule
